# Fritzing sketch circuit diagram (saved by Fritzing 0.9.3b)

parts:
  MH-ET_LIVE_ESP32_DEVKIT1 = MH-ET LIVE ESP32 DEVKIT 38 pins
  Bauteil1 = MQ-9 breakout
  S1 = Round Pushbutton
  S2 = Round Pushbutton
  Grove1 = Grove OLED 128x96
  U1 = Sharp Dust Sensor [part_number=GP2Y1010AU0F]
  Sensor1 = Gas Sensor Breakout Board  # not connected
  Bauteil2 = DHT22 module
  A2 = Littlebee 40A ESC
  A3 = DYS BE1806
  R2 = Resistor [tolerance=±1% resistance=2k package=THT]  # not connected
  R3 = Resistor [tolerance=±1% resistance=1k package=THT]
  R6 = Resistor [tolerance=±1% resistance=1k package=THT]  # not connected
  R7 = Resistor [tolerance=±1% resistance=2k package=THT]  # not connected
  R8 = Resistor [tolerance=±0.5% resistance=150 package=THT]
  C1 = Electrolytic Capacitor [capacitance=1µF package="100 mil [THT, electrolytic]"]
  R9 = Resistor [tolerance=±5% resistance=1 package=THT]
  R10 = Resistor [tolerance=±5% resistance=2k package=THT]

nets:
  3V3: MH-ET_LIVE_ESP32_DEVKIT1.3V3, Grove1.VCC
  N1: MH-ET_LIVE_ESP32_DEVKIT1.SVP, R10.Pin_0
  N2: MH-ET_LIVE_ESP32_DEVKIT1.IO25, A2.Pin_8
  N3: MH-ET_LIVE_ESP32_DEVKIT1.5V, A2.Pin_7, R8.Pin_1
  GND: MH-ET_LIVE_ESP32_DEVKIT1.GND, S2.leg0, Grove1.GND, Bauteil2.GND, A2.Pin_6
  N4: MH-ET_LIVE_ESP32_DEVKIT1.IO23, U1.LED
  N5: MH-ET_LIVE_ESP32_DEVKIT1.IO22, Grove1.SCL
  N6: MH-ET_LIVE_ESP32_DEVKIT1.IO21, Grove1.SDA
  N7: MH-ET_LIVE_ESP32_DEVKIT1.IO19, S2.leg1
  N8: MH-ET_LIVE_ESP32_DEVKIT1.IO18, S1.leg1
  N9: MH-ET_LIVE_ESP32_DEVKIT1.IO4, Bauteil2.DATA
  N10: Bauteil1.AO, R3.Pin_0
  N11: U1.V-LED, R8.Pin_0, C1.+
  N12: U1.LED-GND, C1.-
  N13: U1.Vo, R9.Pin_0
  N14: A2.Pin_3, A3.Pin_3
  N15: A2.Pin_4, A3.Pin_2
  N16: A2.Pin_5, A3.Pin_1

custom parts:
  MH-ET LIVE ESP32 DEVKIT 38 pins: http://mh.nodebb.com/topic/2/mh-et-live-esp32-devkit
  MQ-9 breakout: SKU: 101284
  Sharp Dust Sensor: Sharp GP2Y1010AU0F Dust Sensor
  Gas Sensor Breakout Board: Gas sensor breakout board. Input voltage is 5V. Sensor output is available in analog and digital.
  Littlebee 40A ESC: LittleBee 40A 2-4 LiPo Battery ESC Brushless Speed Controller for RC FPV Multicopter.
  DYS BE1806: quadcopter brushless motor.

// code stored in the sketch: Untitled.ino
hello world
